# Fritzing sketch ConstantCurrent_DummyLoad (saved by Fritzing 0.9.3b)
breadboards: 2

parts:
  U1 = LM124-324 Quad Opamp [package="DIP (Dual Inline)"]
  RV2 = TRIMPOT [part_number=10K package=trimpot_pth_s3_lock]
  F1 = Fan - Ventilador [package=THT]
  Part1 = LCD1602-I2C
  Part2 = Arduino Nano (Rev3.0) (ICSP)
  Q1 = MOSFET-NCHANNEL [part_number=BS170 package=to-92]
  Q3 = Basic FET P-Channel [part_number=50N06 package="TO220 [THT]"]
  D1 = Rectifier Diode [part_number=1N4001 package="300 mil [THT]"]
  D2 = Rectifier Diode [part_number=1N4001 package="300 mil [THT]"]
  D3 = Rectifier Diode [part_number=1N4001 package="300 mil [THT]"]
  D4 = Rectifier Diode [part_number=1N4001 package="300 mil [THT]"]
  D5 = Rectifier Diode [part_number=1N4001 package="300 mil [THT]"]
  BAT1 = BC9VPC [package=bc9vpc]
  IC1 = Voltage Regulator [part_number=7812 package=to-220-alt]
  C4 = Electrolytic Capacitor [capacitance=100µF package="200 mil [THT, electrolytic]"]
  C1 = Capacitor [part_number=100uF package=cap-pth-small2]
  C7 = Capacitor [part_number=100uF package=cap-pth-small2]
  R3 = Resistor [tolerance=±5% resistance=47k power=0.25W package=THT]
  TH1 = Temperature Sensor (Thermistor) [thermistor_type=NTC package=THT]
  R8 = Resistor [tolerance=±5% resistance=10 power=0.25W package=THT]
  R4 = Resistor [tolerance=±5% resistance=150k power=0.25W package=THT]
  LED_Temp = LEDs [package=led10mm]
  Q4 = MOSFET-NCHANNEL [part_number=BS170 package=to-92]
  R9 = Resistor [tolerance=±5% resistance=1k power=0.25W package=THT]
  RV0 = TRIMPOT [part_number=20K package=trimpot_pth_s3_lock]
  JP1 = Header 2 [package=molex-1x2_lock]
  JP2 = Header 4 [package=molex-1x4_lock]
  JP3 = Header 4 [package=molex-1x4_lock]
  R10 = Resistor [tolerance=±10% resistance=100k power=0.25W package=THT]
  R11 = Resistor [tolerance=±5% resistance=1 power=3W package=THT]
  R12 = Resistor [tolerance=±5% resistance=1 power=3W package=THT]
  R13 = Resistor [tolerance=±5% resistance=1 power=3W package=THT]
  R14 = Resistor [tolerance=±5% resistance=1 power=3W package=THT]
  R15 = Resistor [tolerance=±5% resistance=1 power=3W package=THT]
  R16 = Resistor [tolerance=±5% resistance=1 power=3W package=THT]
  R17 = Resistor [tolerance=±5% resistance=1 power=3W package=THT]
  R18 = Resistor [tolerance=±5% resistance=1 power=3W package=THT]
  R19 = Resistor [tolerance=±5% resistance=1 power=3W package=THT]
  R20 = Resistor [tolerance=±5% resistance=1 power=3W package=THT]
  R6 = Resistor [tolerance=±5% resistance=470 power=0.25W package=THT]
  C8 = Tantalum Capacitor [capacitance=100nF package="C 6032 [SMD, tantalum]"]
  MOV1 = VA250LA40BP [part_number="50V MOV" package=VA250LA40BP]
  JP4 = Header 2 [package=molex-1x2_lock]
  Q5 = Basic FET P-Channel [part_number=50N06 package="TO220 [THT]"]
  R21 = Resistor [tolerance=±5% resistance=470 power=0.25W package=THT]
  C9 = Tantalum Capacitor [capacitance=100nF package="C 6032 [SMD, tantalum]"]
  R22 = Resistor [tolerance=±5% resistance=1k power=0.25W package=THT]
  C11 = Capacitor [part_number=100uF package=cap-pth-small2]
  RV3 = TRIMPOT [part_number=10K package=trimpot_pth_s3_lock]
  LED_FAN = LEDs [package=led10mm]
  R23 = Resistor [tolerance=±5% resistance=1k power=0.25W package=THT]
  LED_PWR = LEDs [package=led10mm]
  R24 = Resistor [tolerance=±5% resistance=1k power=0.25W package=THT]
  JP5 = Header 2 [package=molex-1x2_lock]
  JP6 = Header 2 [package=molex-1x2_lock]
  JP7 = Header 2 [package=molex-1x2_lock]
  Fuse1 = Fuse with Handler [part_number="Htc-15m - 700mA Fuse"]
  JP8 = Header 2 [package=molex-1x2_lock]
  C3 = Electrolytic Capacitor [capacitance=1μF package="100 mil [THT, electrolytic]"]
  C12 = Electrolytic Capacitor [capacitance=100µF package="200 mil [THT, electrolytic]"]

nets:
  N1: U1.1OUT, LED_Temp.A, Q4.G, JP7.1
  N2: U1.1IN-, U1.2IN-, TH1.pin_1, R8.Pin_0, R4.Pin_0
  N3: U1.1IN+, R4.Pin_1, RV0.WIPER
  VCC: U1.VCC+, RV2.CW, Part1.VCC, Part2.VIN, D1.cathode, IC1.OUT, C1.1, R8.Pin_1, RV0.CW, JP2.1, JP3.1, R10.Pin_1, LED_PWR.A, JP6.1, C3.+, C12.-
  N4: U1.2IN+, RV2.WIPER, R3.Pin_0
  N5: U1.2OUT, Q1.G, R3.Pin_1, LED_FAN.A, JP5.1
  GND: U1.VCC-, RV2.CCW, F1.GND, Part1.GND, Part2.GND, Q1.D, D4.anode, D5.anode, IC1.GND, C4.-, C7.1, TH1.pin_0, Q4.D, R9.Pin_0, RV0.CCW, JP2.2, JP3.2, R11.Pin_1, R12.Pin_1, R13.Pin_1, R14.Pin_1, R15.Pin_1, R16.Pin_1, R17.Pin_1, R18.Pin_1, R19.Pin_1, R20.Pin_1, C8.-, MOV1.P$1, JP4.2, C9.-, RV3.CCW, R23.Pin_0, R24.Pin_0, C3.-, C12.+
  N6: U1.4IN+, Q4.S, R10.Pin_0, RV3.WIPER, RV3.CW
  N7: U1.4IN-, R22.Pin_0, C11.2
  N8: F1.5V, Q1.S, D1.anode, C1.2
  N9: Part1.SDA, Part2.A4
  N10: Part1.SCL, Part2.A5
  N11: Part2.D1/TX, JP3.3
  N12: Part2.D0/RX, JP3.4
  N13: Part2.RESET, Part2.5V
  N14: Part2.AREF, JP1.1
  N15: Part2.3V3, JP1.2
  N16: Q3.gate, R6.Pin_0, C8.+
  N17: Q3.drain, R22.Pin_1, C11.1
  N18: Q3.source, R11.Pin_0, R12.Pin_0, R13.Pin_0, R14.Pin_0, R15.Pin_0, R16.Pin_0, R17.Pin_0, R18.Pin_0, R19.Pin_0, R20.Pin_0, Q5.source
  N19: D2.cathode, D3.cathode, IC1.IN, C4.+, C7.2
  N20: D2.anode, D4.cathode, BAT1.V-, JP8.1
  N21: D3.anode, D5.cathode, BAT1.V+, JP8.2
  N22: LED_Temp.C, R9.Pin_1, JP7.2
  N23: R6.Pin_1, R21.Pin_1
  N24: JP4.1, Fuse1.Connector2
  N25: Q5.gate, R21.Pin_0, C9.+
  N26: Q5.drain, Fuse1.Connector1
  N27: LED_FAN.C, R23.Pin_1, JP5.2
  N28: LED_PWR.C, R24.Pin_1, JP6.2

custom parts:
  Fan - Ventilador: Ventilador de 2 pines, se encuentra comunmente en computadoras de escritorio
  LCD1602-I2C: A standard character display, usually with 2x16 characters. Comes in many colors with LCM1602 IIC attached.
  VA250LA40BP: Varistor (V18za2p with hole size increased to .042 and breadboard vuiew fixed up.)
